// Logisim project ALU.circ as structural Verilog: 6 circuits, main circuit main
module main (
  input  Carry_In,
  input  A,
  input  B,
  input  Activator,
  output out_5,
  output Carry
);

  wire and_1_out, and_2_out, xor_1_out, xor_2_out;

  and and_1 (and_1_out, B, A, Activator);
  xor xor_1 (xor_1_out, A, B);
  or or_1 (Carry, and_1_out, and_2_out);
  and and_2 (and_2_out, Activator, xor_1_out, Carry_In);
  xor xor_2 (xor_2_out, Carry_In, xor_1_out);
  and and_3 (out_5, xor_2_out, Activator);
endmodule

module Decoder (
  input  F0,
  input  F1,
  output Enables_AND,
  output Enables_OR,
  output Enables_NOT,
  output Adder
);

  wire not_1_out, not_2_out, not_3_out, not_4_out;

  not not_1 (not_1_out, F0);
  not not_2 (not_2_out, F1);
  not not_3 (not_3_out, F0);
  not not_4 (not_4_out, F1);
  and and_1 (Enables_AND, not_1_out, not_2_out);
  and and_2 (Enables_OR, not_3_out, F1);
  and and_3 (Enables_NOT, F0, not_4_out);
  and and_4 (Adder, F0, F1);

  // Notes on the sheet:
  //   00 - AND
  //   01 - OR
  //   10 - NOT
  //   11 - Adder
endmodule

module Logical_Unit (
  input  A,
  input  B,
  input  in_3,
  input  Enable_Lines,
  input  in_5,
  output out_6,
  output out_7,
  output out_8,
  output out_9,
  output out_10
);

  wire A_B_out, and_1_out, not_1_out;

  and and_1 (and_1_out, A, B);
  or A_B (A_B_out, A, B);
  not not_1 (not_1_out, B);
  and and_2 (out_6, and_1_out, in_3);
  and and_3 (out_7, A_B_out, Enable_Lines);
  and and_4 (out_8, not_1_out, in_5);

  assign out_9 = A;
  assign out_10 = B;

  // Notes on the sheet:
  //   AB
  //   !B
endmodule

module ALU (
  input  Carry_In,
  input  INVA,
  input  A,
  input  ENA,
  input  B,
  input  ENB,
  input  F0,
  input  F1,
  output Output,
  output Carry_Out
);

  wire and_1_out, and_2_out, Decoder_adder, Decoder_enables_and, Decoder_enables_not, Decoder_enables_or,
       Full_Adder_out_5, Logic_Unit_out_6, Logic_Unit_out_7, Logic_Unit_out_8, Logic_Unit_out_9,
       Logic_Unit_out_10, xor_1_out;

  and and_1 (and_1_out, A, ENA);
  and and_2 (and_2_out, B, ENB);
  xor xor_1 (xor_1_out, INVA, and_1_out);
  Decoder Decoder (
    .F0(F0), .F1(F1), .Enables_AND(Decoder_enables_and), .Enables_OR(Decoder_enables_or),
    .Enables_NOT(Decoder_enables_not), .Adder(Decoder_adder));
  Logical_Unit Logic_Unit (
    .A(xor_1_out), .B(and_2_out), .out_9(Logic_Unit_out_9), .out_10(Logic_Unit_out_10),
    .in_3(Decoder_enables_and), .Enable_Lines(Decoder_enables_or), .in_5(Decoder_enables_not),
    .out_6(Logic_Unit_out_6), .out_7(Logic_Unit_out_7), .out_8(Logic_Unit_out_8));
  or or_1 (Output, Logic_Unit_out_6, Logic_Unit_out_7, Logic_Unit_out_8, Full_Adder_out_5);
  main Full_Adder (
    .A(Logic_Unit_out_10), .B(Logic_Unit_out_9), .Activator(Decoder_adder), .Carry_In(Carry_In),
    .Carry(Carry_Out), .out_5(Full_Adder_out_5));

  // Notes on the sheet:
  //   00 - AND
  //   01 - OR
  //   10 - NOT
  //   11 - Adder
endmodule

module _8_bit_ALU (
  input  EnA,
  input  EnB,
  input  [7:0] A,
  input  InvA,
  input  [7:0] B,
  input  F0,
  input  F1,
  output [7:0] out_8
);

  wire alu_1_carry_out, alu_2_carry_out, alu_3_carry_out, alu_4_carry_out, alu_5_carry_out, alu_6_carry_out,
       alu_7_carry_out, alu_8_carry_out;

  ALU alu_1 (
    .INVA(InvA), .A(A[0]), .ENA(EnA), .B(B[0]), .ENB(EnB), .Output(out_8[0]), .Carry_In(alu_8_carry_out),
    .Carry_Out(alu_1_carry_out), .F1(F1), .F0(F0));
  ALU alu_2 (
    .INVA(InvA), .A(A[1]), .ENA(EnA), .B(B[1]), .ENB(EnB), .Output(out_8[1]), .Carry_In(alu_1_carry_out),
    .Carry_Out(alu_2_carry_out), .F1(F1), .F0(F0));
  ALU alu_3 (
    .INVA(InvA), .A(A[2]), .ENA(EnA), .B(B[2]), .ENB(EnB), .Output(out_8[2]), .Carry_In(alu_2_carry_out),
    .Carry_Out(alu_3_carry_out), .F1(F1), .F0(F0));
  ALU alu_4 (
    .INVA(InvA), .A(A[3]), .ENA(EnA), .B(B[3]), .ENB(EnB), .Output(out_8[3]), .Carry_In(alu_3_carry_out),
    .Carry_Out(alu_4_carry_out), .F1(F1), .F0(F0));
  ALU alu_5 (
    .INVA(InvA), .A(A[4]), .ENA(EnA), .B(B[4]), .ENB(EnB), .Output(out_8[4]), .Carry_In(alu_4_carry_out),
    .Carry_Out(alu_5_carry_out), .F1(F1), .F0(F0));
  ALU alu_6 (
    .INVA(InvA), .A(A[5]), .ENA(EnA), .B(B[5]), .ENB(EnB), .Output(out_8[5]), .Carry_In(alu_5_carry_out),
    .Carry_Out(alu_6_carry_out), .F1(F1), .F0(F0));
  ALU alu_7 (
    .INVA(InvA), .A(A[6]), .ENA(EnA), .B(B[6]), .ENB(EnB), .Output(out_8[6]), .Carry_In(alu_6_carry_out),
    .Carry_Out(alu_7_carry_out), .F1(F1), .F0(F0));
  ALU alu_8 (
    .INVA(InvA), .A(A[7]), .ENA(EnA), .B(B[7]), .ENB(EnB), .Output(out_8[7]), .Carry_In(alu_7_carry_out),
    .Carry_Out(alu_8_carry_out), .F1(F1), .F0(F0));

  // Notes on the sheet:
  //   00 - AND
  //   01 - OR
  //   10 - NOT
  //   11 - ADDER
endmodule

module _16_bit_ALU (
  input  InvA,
  input  EnA,
  input  EnB,
  input  [15:0] in_4,
  input  [15:0] in_5,
  input  F0,
  input  F1,
  output [15:0] out_8
);

  _8_bit_ALU u_8_bit_alu_1 (
    .EnA(EnA), .A(in_4[7:0]), .InvA(InvA), .B(in_5[7:0]), .F0(F0), .out_8(out_8[7:0]), .F1(F1), .EnB(EnB));
  _8_bit_ALU u_8_bit_alu_2 (
    .EnA(EnA), .A(in_4[15:8]), .InvA(InvA), .B(in_5[15:8]), .F0(F0), .out_8(out_8[15:8]), .F1(F1), .EnB(EnB));

  // Notes on the sheet:
  //   A
  //   B
  //   00 - AND
  //   01 - OR
  //   10 - NOT B
  //   11 - ADDER
endmodule
